// Logisim project bcd_adder.circ as structural Verilog: 3 circuits, main circuit main
module main (
  input  [3:0] A100,
  input  [3:0] B100,
  input  [3:0] A10,
  input  [3:0] B10,
  input  [3:0] A1,
  input  [3:0] B1,
  input  Cin,
  output [3:0] S100,
  output Cout,
  output [3:0] S10,
  output [3:0] S1
);

  wire Cout1, Cout10;

  bcd_digit digit_100 (.Cin(Cout10), .A(A100), .B(B100), .Cout(Cout), .S(S100));
  bcd_digit digit_10 (.Cin(Cout1), .A(A10), .B(B10), .Cout(Cout10), .S(S10));
  bcd_digit digit_1 (.Cin(Cin), .A(A1), .B(B1), .Cout(Cout1), .S(S1));
  Hex_Digit_Display hex_digit_display_1 (.value(S100));  // open: dp
  LED led_1 (.in(Cout));
  Hex_Digit_Display hex_digit_display_2 (.value(S10));  // open: dp
  Hex_Digit_Display hex_digit_display_3 (.value(S1));  // open: dp
endmodule

module full_adder (
  input  A,
  input  B,
  input  Cin,
  output Sum,
  output Cout
);

  wire P1, P2, X1;

  xor xor_1 (X1, A, B);
  and and_1 (P1, A, B);
  xor xor_2 (Sum, X1, Cin);
  and and_2 (P2, X1, Cin);
  or or_1 (Cout, P1, P2);
endmodule

module bcd_digit (
  input  Cin,
  input  [3:0] A,
  input  [3:0] B,
  output [3:0] S,
  output Cout
);

  wire CoutH, CY0, CY1, CY2, CYC0, CYC1, CYC2, G1OUT, G2OUT, S0, S1, S2, S3;

  full_adder FA3 (.A(A[3]), .B(B[3]), .Cin(CY2), .Sum(S3), .Cout(CoutH));
  full_adder FA2 (.A(A[2]), .B(B[2]), .Cin(CY1), .Sum(S2), .Cout(CY2));
  full_adder FA1 (.A(A[1]), .B(B[1]), .Cin(CY0), .Sum(S1), .Cout(CY1));
  full_adder FA0 (.A(A[0]), .B(B[0]), .Cin(Cin), .Sum(S0), .Cout(CY0));
  or or_1 (G1OUT, S2, S1);
  and and_1 (G2OUT, S3, G1OUT);
  Hex_Digit_Display hex_digit_display_1 (.value(S));  // open: dp
  or or_2 (Cout, CoutH, G2OUT);
  full_adder FAC0 (.A(S0), .B(1'b0), .Cin(1'b0), .Sum(S[0]), .Cout(CYC0));
  full_adder FAC1 (.A(S1), .B(Cout), .Cin(CYC0), .Sum(S[1]), .Cout(CYC1));
  full_adder FAC2 (.A(S2), .B(Cout), .Cin(CYC1), .Sum(S[2]), .Cout(CYC2));
  full_adder FAC3 (.A(S3), .B(1'b0), .Cin(CYC2), .Sum(S[3]));  // open: Cout

  // Other names for the same wires on the sheet: A4[3:0] = A; B4[3:0] = B; CORR = Cout; SD0 = S[0]; SOUT4[3:0] = S;
  //   SD1 = S[1]; SD2 = S[2]; SD3 = S[3]
endmodule
